# Fritzing sketch schematic (saved by Fritzing 0.9.3b)
breadboards: 1

parts:
  Adafruit_HUZZAH_ESP8266_Breakout1 = Adafruit HUZZAH ESP8266 Breakout [part_number=2471]
  LED1 = LED - 5mm [color="Red (633nm)" package="5 mm [THT]"]
  LED2 = LED - 5mm [color="Green (565nm)" package="5 mm [THT]"]
  R1 = Resistor [tolerance=±5% resistance=330 package=THT]
  R2 = Resistor [tolerance=±5% resistance=330 package=THT]
  DHT1 = DHT11 Humitidy and Temperature Sensor (3 pins)
  R3 = Resistor [tolerance=±5% resistance=10k package=THT]
  R4 = PHOTOCELL [package=photocell-kit]

nets:
  GND: Adafruit_HUZZAH_ESP8266_Breakout1.GND, R1.Pin_1, DHT1.GND, R3.Pin_1
  N1: Adafruit_HUZZAH_ESP8266_Breakout1.#16, R2.Pin_0, DHT1.VDD
  N2: Adafruit_HUZZAH_ESP8266_Breakout1.A, R3.Pin_0, R4.P$1
  N3: Adafruit_HUZZAH_ESP8266_Breakout1.#5, LED2.anode
  N4: Adafruit_HUZZAH_ESP8266_Breakout1.#4, LED1.anode
  N5: Adafruit_HUZZAH_ESP8266_Breakout1.3V, R2.Pin_1, DHT1.DATA, R4.P$2
  N6: LED1.cathode, LED2.cathode, R1.Pin_0

custom parts:
  DHT11 Humitidy and Temperature Sensor (3 pins): DHT11 Humidity and Temperature Sensor (3 pins) from the design created by John De Cristofaro for Adafruit Industries.
